# Fritzing sketch Bluetooth mod (saved by Fritzing 0.9.3b)
breadboards: 1

parts:
  Part2 = Adafruit Bluefruit LE SPI Friend [part_number="Adafruit #2633"]
  Part3 = Arduino Uno (Rev3)

nets:
  N1: Part2.SCK, Part3.D13/SCK
  N2: Part2.MISO, Part3.D12/MISO
  N3: Part2.MOSI, Part3.D11_PWM/MOSI
  N4: Part2.CS, Part3.D10_PWM/SS
  N5: Part2.IRQ, Part3.D2
  N6: Part2.RST, Part3.D9_PWM
  GND: Part2.GND, Part3.GND
  VIN: Part2.VIN, Part3.5V

custom parts:
  Adafruit Bluefruit LE SPI Friend: The Bluefruit LE SPI Friend makes it easy to add Bluetooth Low Energy connectivity to anything with 4 or 5 GPIO pins. With SPI, you don't have to worry about baud rates, flow control, or giving up a hardware UART port. Connect to your Arduino or other microcontroller using the common four-pin SPI interface (MISO, MOSI, SCK and CS) plus a 5th GPIO pin for interrupts (to let the Arduino know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
