# Fritzing sketch Main Circuit March 1 (saved by Fritzing 0.9.3b)

parts:
  Part1 = Arduino Motor Shield (Rev3)
  M1 = DC Motor
  M2 = DC Motor
  VCC1 = 4 x AAA Battery Mount
  Part2 = Arduino Uno (Rev3)  # not connected

nets:
  N1: Part1.B-, M2.pin_2
  N2: Part1.B+, M2.pin_1
  N3: Part1.A-, M1.pin_2
  N4: Part1.A+, M1.pin_1
  N5: Part1.VMOT, VCC1.+
  N6: Part1.GND, VCC1.-
